// Logisim project Q0.circ as structural Verilog: 1 circuit, main circuit main
module main (
);

  wire d_ff_1_q, d_ff_1_qn, multiplexer_1_out, undriven, undriven_2, undriven_3, undriven_4, undriven_5,
       undriven_6, undriven_7, undriven_8, undriven_9, undriven_10, undriven_11, undriven_12, undriven_13,
       undriven_14, undriven_15, undriven_16, undriven_18, undriven_19, undriven_20, undriven_21;
  wire [3:0] undriven_17;

  Multiplexer #(.enable("true"), .select(4)) multiplexer_1 (
    .in0(undriven), .in1(undriven_2), .in2(undriven_3), .in3(undriven_4), .in4(undriven_5), .in5(undriven_6),
    .in6(undriven_7), .in7(undriven_8), .in8(undriven_9), .in9(undriven_10), .in10(undriven_11),
    .in11(undriven_12), .in12(undriven_13), .in13(undriven_14), .in14(undriven_15), .in15(undriven_16),
    .out(multiplexer_1_out), .sel(undriven_17), .en(undriven_18));
  D_Flip_Flop d_ff_1 (
    .D(multiplexer_1_out), .clk(undriven_19), .Q(d_ff_1_q), .Qn(d_ff_1_qn), .preset(undriven_20),
    .reset(undriven_21));

  // Notes on the sheet:
  //   !ON_SIGHT
  //   ACT
  //   1
  //   0
  //   DET
  //   0
  //   INST
  //   0
  //   1
  //   STATUS
  //   1
  //   0
  //   0
  //   0
  //   0
  //   1
  //   Q3
  //   Q2
  //   Q1
  //   Q0
  //   D0
  //   CLK
  //   !EN
  //   !EN
  //   1
  //   t+1
  //   Q0
  //   t+1
  //   !Q0
endmodule
