// Logisim project Q1.circ as structural Verilog: 1 circuit, main circuit main
module main (
);

  wire j_k_ff_1_q, j_k_ff_1_qn, nand_1_out, nand_2_out, nand_3_out, nand_4_out, nand_5_out, nand_6_out,
       nand_7_out, nand_8_out, nand_9_out, nand_10_out, nand_11_out, nand_12_out, nor_1_out, nor_2_out,
       nor_3_out, nor_4_out, nor_5_out, nor_6_out, nor_7_out, nor_8_out, undriven, undriven_2, undriven_3,
       undriven_4, undriven_5, undriven_6, undriven_7, undriven_8, undriven_9, undriven_10, undriven_11,
       undriven_12, undriven_13, undriven_14, undriven_15, undriven_16, undriven_17, undriven_18,
       undriven_19, undriven_20, undriven_21, undriven_22, undriven_23, undriven_24, undriven_25,
       undriven_26, undriven_27;

  nand nand_1 (nand_1_out, undriven_2, undriven_2);
  nand nand_2 (nand_2_out, undriven_3, undriven_3);
  nand nand_3 (nand_3_out, undriven_4, undriven_4);
  nand nand_4 (nand_4_out, undriven_7, undriven_7);
  nand nand_5 (nand_5_out, undriven_8, undriven_8);
  nand nand_6 (nand_6_out, undriven_9, undriven_9);
  nand nand_7 (nand_7_out, undriven_10, undriven_10);
  nor nor_1 (nor_1_out, undriven_11, undriven_12, undriven_13);
  nor nor_2 (nor_2_out, undriven_14, undriven_14);
  nor nor_3 (nor_3_out, undriven_15, undriven_15);
  nor nor_4 (nor_4_out, undriven_16, undriven_17, undriven_18);
  nor nor_5 (nor_5_out, undriven_19, undriven_20, undriven_21);
  nand nand_8 (nand_8_out, undriven, nand_1_out);
  nand nand_9 (nand_9_out, nand_2_out, nand_3_out, undriven_23);
  nand nand_10 (nand_10_out, undriven_5, undriven_6, nand_4_out);
  nand nand_11 (nand_11_out, nand_5_out, nand_6_out, undriven_24, nand_7_out);
  nor nor_6 (nor_6_out, nor_2_out, undriven_22, nor_3_out);
  nand nand_12 (nand_12_out, nand_8_out, nand_9_out, nand_10_out, nand_11_out);
  nor nor_7 (nor_7_out, nor_1_out, nor_6_out, nor_4_out, nor_5_out);
  nor nor_8 (nor_8_out, nor_7_out, nor_7_out);
  J_K_Flip_Flop j_k_ff_1 (
    .J(nand_12_out), .K(nor_8_out), .clk(undriven_25), .Q(j_k_ff_1_q), .Qn(j_k_ff_1_qn),
    .preset(undriven_26), .reset(undriven_27));

  // Notes on the sheet:
  //   Q3
  //   Q2
  //   MAN
  //   Q2
  //   Q0
  //   STATUS
  //   Q3
  //   Q0
  //   T_O
  //   Q3
  //   Q2
  //   Q0
  //   Q3
  //   Q2
  //   Q0
  //   Q3
  //   Q2
  //   Q0
  //   DET
  //   Q3
  //   Q2
  //   CAN_FIRE
  //   Q3
  //   Q0
  //   J1
  //   K1
  //   !EN
  //   1
  //   CLK
  //   t+1
  //   Q1
  //   t+1
  //   !Q1
endmodule
