// Logisim project Q2.circ as structural Verilog: 1 circuit, main circuit main
module main (
);

  wire and_1_out, and_2_out, and_3_out, and_4_out, and_5_out, and_6_out, and_7_out, and_8_out, and_9_out,
       d_ff_1_q, d_ff_1_qn, multiplexer_1_out, not_1_out, not_2_out, not_3_out, not_4_out, not_5_out,
       not_6_out, not_7_out, not_8_out, not_9_out, not_10_out, not_11_out, or_1_out, or_2_out, undriven,
       undriven_2, undriven_3, undriven_4, undriven_5, undriven_6, undriven_7, undriven_8, undriven_9,
       undriven_10, undriven_11, undriven_12, undriven_13, undriven_14, undriven_15, undriven_16,
       undriven_17, undriven_18, undriven_19, undriven_20, undriven_21, undriven_22, undriven_23,
       undriven_24, undriven_25, undriven_26, undriven_27, undriven_28, undriven_29, undriven_30,
       undriven_31, undriven_32;

  not not_1 (not_1_out, undriven_4);
  not not_2 (not_2_out, undriven_6);
  not not_3 (not_3_out, undriven_8);
  not not_4 (not_4_out, undriven_11);
  not not_5 (not_5_out, undriven_12);
  not not_6 (not_6_out, undriven_17);
  not not_7 (not_7_out, undriven_21);
  not not_8 (not_8_out, undriven_22);
  not not_9 (not_9_out, undriven_23);
  not not_10 (not_10_out, undriven_24);
  not not_11 (not_11_out, undriven_27);
  and and_1 (and_1_out, undriven, undriven_2, undriven_3);
  and and_2 (and_2_out, not_1_out, undriven_5, not_2_out);
  and and_3 (and_3_out, undriven_7, not_3_out, undriven_9);
  and and_4 (and_4_out, undriven_10, not_4_out, not_5_out, undriven_13);
  and and_5 (and_5_out, undriven_14, undriven_15, undriven_16);
  and and_6 (and_6_out, not_6_out, undriven_18, undriven_19);
  and and_7 (and_7_out, undriven_20, not_7_out);
  and and_8 (and_8_out, not_8_out, not_9_out, not_10_out);
  and and_9 (and_9_out, undriven_25, undriven_26, not_11_out);
  or or_1 (or_1_out, and_1_out, and_2_out, and_3_out, and_4_out, and_5_out);
  or or_2 (or_2_out, and_6_out, and_7_out, and_8_out, and_9_out);
  D_Flip_Flop d_ff_1 (
    .D(multiplexer_1_out), .clk(undriven_30), .Q(d_ff_1_q), .Qn(d_ff_1_qn), .preset(undriven_31),
    .reset(undriven_32));
  Multiplexer #(.enable("true")) multiplexer_1 (
    .in0(or_1_out), .in1(or_2_out), .out(multiplexer_1_out), .sel(undriven_28), .en(undriven_29));

  // Notes on the sheet:
  //   Q2
  //   Q1
  //   Q0
  //   Q2
  //   Q1
  //   Q0
  //   DET
  //   Q2
  //   Q1
  //   MAN
  //   Q2
  //   Q1
  //   Q0
  //   INST
  //   Q2
  //   Q0
  //   Q2
  //   Q1
  //   Q0
  //   Q2
  //   Q0
  //   STATUS
  //   Q1
  //   Q0
  //   ON_SIGHT
  //   Q1
  //   Q0
  //   D2
  //   !EN
  //   Q3
  //   CLK
  //   !EN
  //   1
  //   t+1
  //   Q2
  //   t+1
  //   !Q2
endmodule
