// Logisim project Q3.circ as structural Verilog: 1 circuit, main circuit main
module main (
);

  wire and_1_out, and_2_out, and_3_out, and_4_out, j_k_ff_1_q, j_k_ff_1_qn, multiplexer_1_out,
       multiplexer_2_out, not_1_out, not_2_out, not_3_out, not_4_out, or_1_out, undriven, undriven_2,
       undriven_3, undriven_4, undriven_5, undriven_6, undriven_7, undriven_8, undriven_9, undriven_10,
       undriven_11, undriven_12, undriven_13, undriven_14, undriven_15, undriven_16, undriven_17,
       undriven_20, undriven_21, undriven_22, undriven_23, undriven_24;
  wire [1:0] undriven_18;
  wire [2:0] undriven_19;

  not not_1 (not_1_out, undriven_2);
  and and_1 (and_1_out, undriven_3, undriven_4);
  and and_2 (and_2_out, undriven_5, undriven_6);
  not not_2 (not_2_out, undriven_7);
  not not_3 (not_3_out, undriven_8);
  not not_4 (not_4_out, undriven_9);
  and and_3 (and_3_out, undriven, not_1_out);
  and and_4 (and_4_out, not_2_out, not_3_out);
  or or_1 (or_1_out, and_1_out, and_2_out);
  Multiplexer #(.enable("true"), .select(2)) multiplexer_1 (
    .in0(and_3_out), .in1(or_1_out), .in2(undriven_16), .in3(undriven_17), .out(multiplexer_1_out),
    .sel(undriven_18), .en(undriven_20));
  Multiplexer #(.enable("true"), .select(3)) multiplexer_2 (
    .in0(undriven_11), .in1(undriven_12), .in2(undriven_13), .in3(undriven_14), .in4(undriven_10),
    .in5(undriven_15), .in6(and_4_out), .in7(not_4_out), .out(multiplexer_2_out), .sel(undriven_19),
    .en(undriven_21));
  J_K_Flip_Flop j_k_ff_1 (
    .J(multiplexer_1_out), .K(multiplexer_2_out), .clk(undriven_22), .Q(j_k_ff_1_q), .Qn(j_k_ff_1_qn),
    .preset(undriven_23), .reset(undriven_24));

  // Notes on the sheet:
  //   STATUS
  //   Q1
  //   Q0
  //   Q1
  //   Q0
  //   INST
  //   Q0
  //   Q0
  //   Q0
  //   0
  //   0
  //   0
  //   0
  //   0
  //   0
  //   0
  //   Q3
  //   1
  //   Q3
  //   !EN
  //   Q2
  //   Q2
  //   Q1
  //   J3
  //   K3
  //   CLK
  //   !EN
  //   !EN
  //   Q3
  //   !Q3
  //   1
  //   t+1
  //   t+1
endmodule
