// Logisim project full.circ as structural Verilog: 1 circuit, main circuit main
module main (
);

  wire and_1_out, and_2_out, and_3_out, and_4_out, and_5_out, and_6_out, and_7_out, and_8_out, and_9_out,
       and_10_out, and_11_out, and_12_out, and_13_out, d_ff_1_qn, d_ff_2_qn, decoder_1_out0, decoder_1_out1,
       decoder_1_out2, decoder_1_out3, decoder_1_out4, decoder_1_out5, decoder_1_out6, decoder_1_out7,
       decoder_1_out8, decoder_1_out9, decoder_1_out10, decoder_1_out11, decoder_1_out12, decoder_1_out13,
       decoder_1_out14, decoder_1_out15, j_k_ff_1_qn, j_k_ff_2_qn, multiplexer_1_out, multiplexer_2_out,
       multiplexer_3_out, multiplexer_4_out, nand_1_out, nand_2_out, nand_3_out, nand_4_out, nand_5_out,
       nand_6_out, nand_7_out, nor_1_out, nor_2_out, nor_3_out, nor_4_out, nor_5_out, nor_6_out, not_1_out,
       not_2_out, not_3_out, not_4_out, not_5_out, not_6_out, not_7_out, not_8_out, not_9_out, not_10_out,
       or_1_out, or_2_out, or_3_out, undriven, undriven_2, undriven_3, undriven_4, undriven_5, undriven_6,
       undriven_7, undriven_8, undriven_9, undriven_10, undriven_11, undriven_12, undriven_13, undriven_14,
       undriven_15, undriven_16, undriven_17, undriven_18, undriven_19, undriven_20, undriven_21,
       undriven_22, undriven_23, undriven_24, undriven_25, undriven_26, undriven_27, undriven_28,
       undriven_29, undriven_30, undriven_31, undriven_32, undriven_33;
  wire [3:0] d_ff_1_q;

  not not_1 (not_1_out, undriven_2);
  not not_2 (not_2_out, undriven_3);
  and and_1 (and_1_out, d_ff_1_q[1], d_ff_1_q[0]);
  and and_2 (and_2_out, undriven_4, d_ff_1_q[0]);
  not not_3 (not_3_out, undriven_3);
  nand nand_1 (nand_1_out, undriven_5, undriven_5);
  nand nand_2 (nand_2_out, undriven_8, undriven_8);
  nor nor_1 (nor_1_out, d_ff_1_q[3], d_ff_1_q[2], d_ff_1_q[0]);
  nor nor_2 (nor_2_out, undriven_6, d_ff_1_q[3], d_ff_1_q[2]);
  nor nor_3 (nor_3_out, undriven, d_ff_1_q[3], d_ff_1_q[0]);
  and and_3 (and_3_out, d_ff_1_q[2], d_ff_1_q[1], d_ff_1_q[0]);
  and and_4 (and_4_out, d_ff_2_qn, d_ff_1_q[1], d_ff_1_qn);
  and and_5 (and_5_out, undriven_6, d_ff_2_qn, d_ff_1_q[1]);
  and and_6 (and_6_out, undriven_5, d_ff_2_qn, j_k_ff_2_qn, d_ff_1_q[0]);
  and and_7 (and_7_out, undriven_4, d_ff_1_q[2], d_ff_1_q[0]);
  and and_8 (and_8_out, d_ff_2_qn, d_ff_1_q[1], d_ff_1_q[0]);
  and and_9 (and_9_out, d_ff_1_q[2], d_ff_1_qn);
  and and_10 (and_10_out, not_2_out, j_k_ff_2_qn, d_ff_1_qn);
  and and_11 (and_11_out, undriven_2, d_ff_1_q[1], d_ff_1_qn);
  and and_12 (and_12_out, d_ff_1_q[1], d_ff_1_qn);
  and and_13 (and_13_out, not_3_out, d_ff_1_qn);
  Multiplexer #(.enable("true"), .select(4)) multiplexer_1 (
    .in0(undriven_7), .in1(undriven_11), .in2(undriven_12), .in3(undriven_6), .in4(undriven_13),
    .in5(undriven_4), .in6(undriven_14), .in7(undriven_15), .in8(undriven_3), .in9(undriven_16),
    .in10(not_1_out), .in11(undriven_17), .in12(undriven_18), .in13(undriven_19), .in14(undriven_20),
    .in15(undriven_21), .out(multiplexer_1_out), .sel(d_ff_1_q), .en(undriven_9));
  nand nand_3 (nand_3_out, d_ff_1_q[3], d_ff_2_qn);
  nand nand_4 (nand_4_out, nand_1_out, d_ff_2_qn, d_ff_1_q[0]);
  nand nand_5 (nand_5_out, undriven_3, d_ff_1_q[3], d_ff_1_qn);
  nand nand_6 (nand_6_out, nand_2_out, j_k_ff_1_qn, d_ff_1_q[2], d_ff_1_qn);
  or or_1 (or_1_out, and_1_out, and_2_out);
  D_Flip_Flop d_ff_1 (
    .D(multiplexer_1_out), .clk(undriven_10), .Q(d_ff_1_q[0]), .Qn(d_ff_1_qn), .preset(undriven_9),
    .reset(undriven_30));
  nor nor_4 (nor_4_out, j_k_ff_1_qn, d_ff_1_q[2], d_ff_1_qn);
  or or_2 (or_2_out, and_3_out, and_4_out, and_5_out, and_6_out, and_7_out);
  or or_3 (or_3_out, and_8_out, and_9_out, and_10_out, and_11_out);
  Multiplexer #(.enable("true"), .select(2)) multiplexer_2 (
    .in0(and_12_out), .in1(or_1_out), .in2(undriven_28), .in3(undriven_29), .out(multiplexer_2_out),
    .sel(d_ff_1_q[3:2]), .en(undriven_9));
  Multiplexer #(.enable("true"), .select(3)) multiplexer_3 (
    .in0(undriven_23), .in1(undriven_24), .in2(undriven_25), .in3(undriven_26), .in4(undriven_22),
    .in5(undriven_27), .in6(and_13_out), .in7(d_ff_1_qn), .out(multiplexer_3_out), .sel(d_ff_1_q[3:1]),
    .en(undriven_9));
  nand nand_7 (nand_7_out, nand_3_out, nand_4_out, nand_5_out, nand_6_out);
  nor nor_5 (nor_5_out, nor_1_out, nor_4_out, nor_2_out, nor_3_out);
  D_Flip_Flop d_ff_2 (
    .D(multiplexer_4_out), .clk(undriven_10), .Q(d_ff_1_q[2]), .Qn(d_ff_2_qn), .preset(undriven_9),
    .reset(undriven_31));
  Multiplexer #(.enable("true")) multiplexer_4 (
    .in0(or_2_out), .in1(or_3_out), .out(multiplexer_4_out), .sel(d_ff_1_q[3]), .en(undriven_9));
  nor nor_6 (nor_6_out, nor_5_out, nor_5_out);
  J_K_Flip_Flop j_k_ff_1 (
    .J(multiplexer_2_out), .K(multiplexer_3_out), .clk(undriven_10), .Q(d_ff_1_q[3]), .Qn(j_k_ff_1_qn),
    .preset(undriven_9), .reset(undriven_32));
  J_K_Flip_Flop j_k_ff_2 (
    .J(nand_7_out), .K(nor_6_out), .clk(undriven_10), .Q(d_ff_1_q[1]), .Qn(j_k_ff_2_qn), .preset(undriven_9),
    .reset(undriven_33));
  Decoder #(.enable("false"), .select(4)) decoder_1 (
    .out0(decoder_1_out0), .out1(decoder_1_out1), .out2(decoder_1_out2), .out3(decoder_1_out3),
    .out4(decoder_1_out4), .out5(decoder_1_out5), .out6(decoder_1_out6), .out7(decoder_1_out7),
    .out8(decoder_1_out8), .out9(decoder_1_out9), .out10(decoder_1_out10), .out11(decoder_1_out11),
    .out12(decoder_1_out12), .out13(decoder_1_out13), .out14(decoder_1_out14), .out15(decoder_1_out15),
    .sel(d_ff_1_q));
  not not_4 (not_4_out, decoder_1_out2);
  not not_5 (not_5_out, decoder_1_out7);
  not not_6 (not_6_out, decoder_1_out9);
  not not_7 (not_7_out, decoder_1_out10);
  not not_8 (not_8_out, decoder_1_out11);
  not not_9 (not_9_out, decoder_1_out13);
  not not_10 (not_10_out, decoder_1_out15);

  // Notes on the sheet:
  //   CAN_FIRE
  //   ON_SIGHT
  //   STATUS
  //   INST
  //   MAN
  //   DET
  //   ACT
  //   T_O
  //   Q3
  //   Q2
  //   Q1
  //   Q0
  //   !Q3
  //   !Q2
  //   !Q1
  //   !Q0
  //   !EN
  //   CLK
  //   0
  //   0
  //   1
  //   1
  //   0
  //   0
  //   0
  //   0
  //   1
  //   1
  //   0
  //   D0
  //   0
  //   0
  //   0
  //   0
  //   0
  //   1
  //   0
  //   0
  //   1
  //   t+1
  //   Q0
  //   !Q0
  //   t+1
  //   D2
  //   1
  //   J3
  //   K3
  //   J1
  //   Q2
  //   !Q2
  //   Q3
  //   1
  //   K1
  //   t+1
  //   t+1
  //   t+1
  //   t+1
  //   !Q3
  //   1
  //   t+1
  //   Q1
  //   t+1
  //   !Q1
  //   0
  //   0
  //   0
  //   0
  //   0
  //   FIRE
  //   DAT
  //   DAT
  //   LOG
  //   LOG
  //   RCV
  //   LOG
endmodule
